# Fritzing sketch webled (saved by Fritzing 0.9.6b)
breadboards: 1

parts:
  A1 = XIAO ESP32C3-tht
  R1 = Resistor [tolerance=±5% power=0.25 resistance=1k package=THT]
  LED1 = LED - 5mm [color="Red (633nm)" current=0.030 package="5 mm [THT]"]

nets:
  N1: A1.Pin_19, R1.Pin_0
  N2: A1.Pin_21, LED1.cathode
  N3: R1.Pin_1, LED1.anode

custom parts:
  XIAO ESP32C3-tht: Seeed Studio XIAO ESP32C3 adopts new RISC-V architecture, supporting both Wi-Fi and BLE wireless connectivities.
